# Fritzing sketch meteo (saved by Fritzing 0.9.3b)
circuit board: 2.97671cm x 3.24859cm
breadboards: 1

parts:
  Pressure_sensor = Barometric Pressure Sensor - BMP180 Breakout (GY-68)
  DS1 = DS18B20 1-Wire Temperature Sensor [part_number=DS18B20]
  R1 = Resistor [tolerance=±5% resistance=4.7k package=THT]
  Humidity_sensor = Humidity and Temperature Sensor RHT03
  R2 = Resistor [tolerance=±5% resistance=4.7k package=THT]
  R3 = Resistor [tolerance=±5% resistance=1k package=THT]
  WeMos_D1_Mini1 = WeMos D1 Mini
  LED1 = LED - 3mm [color="Red (633nm)" package="3 mm [THT]"]

nets:
  5V: Pressure_sensor.VCC, DS1.VDD, R1.Pin_1, Humidity_sensor.Vcc, R2.Pin_0, WeMos_D1_Mini1.5V
  GND: Pressure_sensor.GND, DS1.GND, Humidity_sensor.GND_1, WeMos_D1_Mini1.G, LED1.cathode
  N1: Pressure_sensor.SCL, WeMos_D1_Mini1.D1
  N2: Pressure_sensor.SDA, WeMos_D1_Mini1.D2
  N3: DS1.DQ, R1.Pin_0, WeMos_D1_Mini1.D4
  N4: Humidity_sensor.Data-signal, R2.Pin_1, WeMos_D1_Mini1.D7
  N5: R3.Pin_0, WeMos_D1_Mini1.D0
  N6: R3.Pin_1, LED1.anode
